// Logisim project ex1.circ as structural Verilog: 6 circuits, main circuit NOR1
module NAND1 (
  input  A,
  input  B,
  output RESULT
);


  // Notes on the sheet:
  //   PUT CIRCUITRY HERE
endmodule

module NOR1 (
  input  A,
  input  B,
  output RESULT
);


  // Notes on the sheet:
  //   PUT CIRCUITRY HERE
endmodule

module XOR1 (
  input  A,
  input  B,
  output RESULT
);


  // Notes on the sheet:
  //   PUT CIRCUITRY HERE
endmodule

module MUX2 (
  input  A,
  input  B,
  input  Sel,
  output RESULT
);


  // Notes on the sheet:
  //   PUT CIRCUITRY HERE
endmodule

module MUX4 (
  input  A,
  input  B,
  input  C,
  input  D,
  input  Sel1,
  input  Sel2,
  output RESULT
);


  // Notes on the sheet:
  //   PUT CIRCUITRY HERE
endmodule

module Half_Adder (
  input  A,
  input  B,
  output SUM,
  output CARRY
);
endmodule
