// Logisim project ex1.circ as structural Verilog: 1 circuit, main circuit Split
module Split (
  input  [7:0] IN1,
  output OUT1,
  output OUT2,
  output [8:0] OUT3,
  output [8:0] OUT4,
  output [7:0] out_6,
  output [8:0] out_7,
  output [8:0] out_8,
  output [8:0] out_9
);

  wire not_1_out, xor_1_out, xor_2_out, xor_3_out, xor_4_out, xor_5_out, xor_6_out;
  wire [3:0] bitadder_1_out;
  wire [7:0] adder_2_out, bit_extender_3_out, not_2_out;
  wire [8:0] bit_extender_1_out, bit_extender_2_out, shifter_1_out;

  xor xor_1 (xor_1_out, IN1[0], IN1[1]);
  xor xor_2 (xor_2_out, IN1[2], IN1[3]);
  xor xor_3 (xor_3_out, IN1[4], IN1[5]);
  xor xor_4 (xor_4_out, IN1[6], IN1[7]);
  not not_1 (not_1_out, OUT1);
  xor xor_5 (xor_5_out, xor_1_out, xor_2_out);
  xor xor_6 (xor_6_out, xor_3_out, xor_4_out);
  assign bit_extender_1_out = {{8{not_1_out}}, not_1_out};  // Bit_Extender bit_extender_1
  assign bit_extender_2_out = {{1{1'b0}}, IN1};  // Bit_Extender bit_extender_2
  xor xor_7 (OUT1, xor_5_out, xor_6_out);
  Shifter #(.width(9)) shifter_1 (.in(bit_extender_1_out), .\dist (4'b1000), .out(shifter_1_out));
  Adder #(.width(9)) adder_1 (.a(shifter_1_out), .b(bit_extender_2_out), .out(OUT3));  // open: cin, cout
  BitAdder bitadder_1 (.in0(IN1), .out(bitadder_1_out));
  Negator negator_1 (.out(out_6));  // open: in
  assign bit_extender_3_out = {{4{1'b0}}, bitadder_1_out};  // Bit_Extender bit_extender_3
  not not_2 (not_2_out[0], IN1[0]);
  not not_3 (not_2_out[1], IN1[1]);
  not not_4 (not_2_out[2], IN1[2]);
  not not_5 (not_2_out[3], IN1[3]);
  not not_6 (not_2_out[4], IN1[4]);
  not not_7 (not_2_out[5], IN1[5]);
  not not_8 (not_2_out[6], IN1[6]);
  not not_9 (not_2_out[7], IN1[7]);
  Adder adder_2 (.a(out_6), .b(8'h1), .out(adder_2_out));  // open: cin, cout
  Comparator comparator_1 (.a(bit_extender_3_out), .b(8'h4), .gt(OUT2));  // open: eq, lt
  Adder #(.width(9)) adder_3 (.a(9'h1), .b({OUT2, not_2_out}), .out(out_9));  // open: cin, cout
  Multiplexer #(.width(9), .enable("false")) multiplexer_1 (.in0({OUT2, IN1}), .in1(out_9), .out(OUT4), .sel(OUT2));

  assign out_7 = {OUT2, IN1};
  assign out_8 = OUT4;

  // Other names for the same wires on the sheet: IN1_0 = IN1[0]; IN1_1 = IN1[1]; IN1_2 = IN1[2]; IN1_3 = IN1[3];
  //   IN1_4 = IN1[4]; IN1_5 = IN1[5]; IN1_6 = IN1[6]; IN1_7 = IN1[7]

  // Notes on the sheet:
  //   PUT CIRCUITRY HERE
endmodule
