// Logisim project ex1.circ as structural Verilog: 4 circuits, main circuit main
module main (
  input  in_1,
  output [7:0] non_pipe_out,
  output [7:0] pipe_out
);

  wire CLK_out;
  wire [7:0] Address_Counter_q, rom_1_data;

  Counter Address_Counter (.clr(in_1), .clk(CLK_out), .Q(Address_Counter_q));  // open: load, up, count, D, carry
  Clock CLK (.out(CLK_out));
  ROM rom_1 (.addr(Address_Counter_q), .data(rom_1_data));
  // Probe on non_pipe_out
  non_pipelined non_pipelined_1 (.in1(rom_1_data[3:0]), .in2(rom_1_data[7:4]), .CLK(CLK_out), .out1(non_pipe_out));
  // Probe on pipe_out
  pipelined pipelined_1 (.in1(rom_1_data[3:0]), .in2(rom_1_data[7:4]), .CLK(CLK_out), .out1(pipe_out));

  // Notes on the sheet:
  //   contents of rom_1 (hex, n*v repeats v):
  //   13 a2 fc 8f 1c 2 b0
endmodule

module non_pipelined (
  input  [3:0] in1,
  input  [3:0] in2,
  input  CLK,
  output [7:0] out1
);

  wire [7:0] move_and_add_1_moved_multiplicand, move_and_add_1_result, move_and_add_2_moved_multiplicand,
       move_and_add_2_result, move_and_add_3_moved_multiplicand, move_and_add_3_result, move_and_add_4_result;

  // Probe on move_and_add_1_result
  move_and_add move_and_add_1 (
    .multiplier(in2[0]), .multiplicand({4'b0000, in1}), .current({8{1'b0}}), .result(move_and_add_1_result),
    .moved_multiplicand(move_and_add_1_moved_multiplicand));
  move_and_add move_and_add_2 (
    .multiplier(in2[1]), .multiplicand(move_and_add_1_moved_multiplicand), .current(move_and_add_1_result),
    .result(move_and_add_2_result), .moved_multiplicand(move_and_add_2_moved_multiplicand));
  move_and_add move_and_add_3 (
    .multiplier(in2[2]), .multiplicand(move_and_add_2_moved_multiplicand), .current(move_and_add_2_result),
    .result(move_and_add_3_result), .moved_multiplicand(move_and_add_3_moved_multiplicand));
  move_and_add move_and_add_4 (
    .multiplier(in2[3]), .multiplicand(move_and_add_3_moved_multiplicand), .current(move_and_add_3_result),
    .result(move_and_add_4_result));  // open: moved_multiplicand
  Register register_1 (.D(move_and_add_4_result), .clk(CLK), .Q(out1));  // open: en, clr

  // Notes on the sheet:
  //   4 * 65 +  Setup + CLK2Q = 4 * 65 + 10 + 10 = 280 ns
  //   f = 1 / 280ns = 3.571 MHz
  //   Longest time = max(Adder, MUX + Adder, Shifter) = 20 + 45 = 65ns 
endmodule

module pipelined (
  input  [3:0] in1,
  input  [3:0] in2,
  input  CLK,
  output [7:0] out1
);

  wire undriven, undriven_2;
  wire [7:0] adder_1_out, move_and_add_1_result, multiplexer_1_out, multiplexer_6_out, register_1_q,
       register_3_q, shifter_1_out, shifter_2_out, shifter_3_out;

  Shifter shifter_1 (.in({4'b0000, in1}), .\dist (3'b001), .out(shifter_1_out));
  Shifter shifter_2 (.in({4'b0000, in1}), .\dist (3'b010), .out(shifter_2_out));
  Register register_1 (.D(multiplexer_1_out), .Q(register_1_q));  // open: en, clk, clr
  Multiplexer #(.width(8), .enable("false")) multiplexer_1 (
    .in0({4'b0000, in1}), .out(multiplexer_1_out), .sel(undriven));  // open: in1
  Multiplexer #(.width(8), .enable("false")) multiplexer_2 (
    .in0({8{1'b0}}), .in1({4'b0000, in1}), .sel(in2[0]));  // open: out
  Multiplexer #(.width(8), .enable("false")) multiplexer_3 (
    .in0({8{1'b0}}), .in1(shifter_1_out), .sel(in2[1]));  // open: out
  Multiplexer #(.width(8), .enable("false")) multiplexer_4 (
    .in0({8{1'b0}}), .in1(shifter_2_out), .sel(in2[2]));  // open: out
  Multiplexer #(.width(8), .enable("false")) multiplexer_5 ();  // open: in0, in1, out, sel
  Shifter shifter_3 (.in(register_1_q), .\dist (3'b001), .out(shifter_3_out));
  Register register_2 (.clk(CLK), .Q(out1));  // open: D, en, clr
  Register register_3 (.D(adder_1_out), .clk(CLK), .Q(register_3_q));  // open: en, clr
  Adder adder_1 (.a(register_3_q), .b(8'h1), .out(adder_1_out));  // open: cin, cout
  Multiplexer #(.width(8), .enable("false")) multiplexer_6 (
    .in0({4'b0000, in1}), .in1(out1), .out(multiplexer_6_out), .sel(undriven_2));
  move_and_add move_and_add_1 (
    .multiplicand(shifter_3_out), .current(multiplexer_6_out), .result(move_and_add_1_result));  // open: multiplier, moved_multiplicand
  Register register_4 (.D(move_and_add_1_result), .clk(CLK), .Q(out1));  // open: en, clr
endmodule

module move_and_add (
  input  [7:0] current,
  input  [7:0] multiplicand,
  input  multiplier,
  output [7:0] result,
  output [7:0] moved_multiplicand
);

  wire [7:0] multiplexer_1_out;

  Multiplexer #(.width(8), .enable("false")) multiplexer_1 (
    .in0({8{1'b0}}), .in1(multiplicand), .out(multiplexer_1_out), .sel(multiplier));
  Adder adder_1 (.a(current), .b(multiplexer_1_out), .out(result));  // open: cin, cout
  Shifter shifter_1 (.in(multiplicand), .\dist (3'b001), .out(moved_multiplicand));

  // Notes on the sheet:
  //   Longest time = max(Adder, MUX + Adder, Shifter) = 20 + 45 = 65ns 
endmodule
