// Logisim project ex1.circ as structural Verilog: 4 circuits, main circuit main
module main (
  output [7:0] non_pipe_out,
  output [7:0] pipe_out
);

  wire CLK_out;
  wire [7:0] Address_Counter_q, rom_1_data;

  Counter Address_Counter (.clk(CLK_out), .Q(Address_Counter_q));  // open: clr, load, up, count, D, carry
  Clock CLK (.out(CLK_out));
  ROM rom_1 (.addr(Address_Counter_q), .data(rom_1_data));
  // Probe on non_pipe_out
  non_pipelined non_pipelined_1 (.in1(rom_1_data[3:0]), .in2(rom_1_data[7:4]), .CLK(CLK_out), .out1(non_pipe_out));
  // Probe on pipe_out
  pipelined pipelined_1 (.in1(rom_1_data[3:0]), .in2(rom_1_data[7:4]), .CLK(CLK_out), .out1(pipe_out));

  // Notes on the sheet:
  //   contents of rom_1 (hex, n*v repeats v):
  //   13 a2 fc 8f 1c 2 13 a2 fc 8f 1c 2 13 a2 fc 8f 1c 2 13 a2 fc 8f 1c 2 13 a2 fc 8f 1c 2 13 a2 fc 8f 1c
  //   2 13 a2 fc 8f 1c 2 13 a2 fc 8f 1c 2 13 a2 fc 8f 1c 2 13 a2 fc 8f 1c 2 13 a2 fc 8f 1c 2 13 a2 fc 8f
  //   1c 2 13 a2 fc 8f 1c 2 13 a2 fc 8f 1c 2 13 a2 fc 8f 1c 2 13 a2 fc 8f 1c 2 13 a2 fc 8f 1c 2 13 a2 fc
  //   8f 1c 13 a2 fc 8f 1c 2 13 a2 fc 8f 1c 2 13 a2 fc 8f 1c 2 13 a2 fc 8f 1c 2 13 a2 fc 8f 1c 2 13 a2 fc
  //   8f 1c 2 13 a2 fc 8f 1c 2 13 a2 fc 8f 1c 2 13 a2 fc 8f 1c 13 a2 fc 8f 1c 2 13 a2 fc 8f 1c 2 13 a2 fc
  //   8f 1c 2 13 a2 fc 8f 1c 2 13 a2 fc 8f 1c 2 13 a2 fc 8f 1c 2 13 a2 fc 8f 1c 2 13 a2 fc 8f 1c 2 13 a2
  //   fc 8f 1c 2 13 a2 fc 8f 1c 2 13 a2 fc 8f 1c 2 13 a2 fc 8f 1c 2 13 a2 fc 8f 1c 2 13 a2 fc 8f 1c 2 13
  //   a2 fc 8f 1c 13 a2 fc 8f 1c aa ea
endmodule

module non_pipelined (
  input  [3:0] in1,
  input  [3:0] in2,
  input  CLK,
  output [7:0] out1
);

  wire [7:0] move_and_add_1_moved_multiplicand, move_and_add_1_result, move_and_add_2_moved_multiplicand,
       move_and_add_2_result, move_and_add_3_moved_multiplicand, move_and_add_3_result, move_and_add_4_result;

  // Probe on move_and_add_1_result
  move_and_add move_and_add_1 (
    .multiplicand({4'b0000, in1}), .result(move_and_add_1_result), .current({8{1'b0}}), .multiplier(in2[0]),
    .moved_multiplicand(move_and_add_1_moved_multiplicand));
  // Probe on move_and_add_2_result
  move_and_add move_and_add_2 (
    .multiplicand(move_and_add_1_moved_multiplicand), .result(move_and_add_2_result),
    .current(move_and_add_1_result), .multiplier(in2[1]),
    .moved_multiplicand(move_and_add_2_moved_multiplicand));
  // Probe on move_and_add_3_result
  move_and_add move_and_add_3 (
    .multiplicand(move_and_add_2_moved_multiplicand), .result(move_and_add_3_result),
    .current(move_and_add_2_result), .multiplier(in2[2]),
    .moved_multiplicand(move_and_add_3_moved_multiplicand));
  move_and_add move_and_add_4 (
    .multiplicand(move_and_add_3_moved_multiplicand), .result(move_and_add_4_result),
    .current(move_and_add_3_result), .multiplier(in2[3]));  // open: moved_multiplicand
  Register register_1 (.D(move_and_add_4_result), .clk(CLK), .Q(out1));  // open: en, clr
  // Probe on move_and_add_4_result
endmodule

module pipelined (
  input  [3:0] in1,
  input  [3:0] in2,
  input  CLK,
  output [7:0] out1
);

  wire [3:0] register_3_q, register_6_q, register_9_q, register_12_q;
  wire [7:0] bit_extender_1_out, move_and_add_1_moved_multiplicand, move_and_add_1_result,
       move_and_add_2_moved_multiplicand, move_and_add_2_result, move_and_add_3_moved_multiplicand,
       move_and_add_3_result, register_1_q, register_2_q, register_4_q, register_5_q, register_7_q,
       register_8_q, register_10_q, register_11_q;

  assign bit_extender_1_out = {{4{1'b0}}, in1};  // Bit_Extender bit_extender_1
  Register register_1 (.D({8{1'b0}}), .clk(CLK), .Q(register_1_q));  // open: en, clr
  Register register_2 (.D(bit_extender_1_out), .clk(CLK), .Q(register_2_q));  // open: en, clr
  Register #(.width(4)) register_3 (.D(in2), .clk(CLK), .Q(register_3_q));  // open: en, clr
  // Probe on register_2_q
  move_and_add move_and_add_1 (
    .multiplicand(register_2_q), .result(move_and_add_1_result), .current(register_1_q),
    .multiplier(register_3_q[0]), .moved_multiplicand(move_and_add_1_moved_multiplicand));
  Register register_4 (.D(move_and_add_1_result), .clk(CLK), .Q(register_4_q));  // open: en, clr
  Register register_5 (.D(move_and_add_1_moved_multiplicand), .clk(CLK), .Q(register_5_q));  // open: en, clr
  Register #(.width(4)) register_6 (.D(register_3_q), .clk(CLK), .Q(register_6_q));  // open: en, clr
  // Probe on register_5_q
  // Probe on register_4_q
  move_and_add move_and_add_2 (
    .multiplicand(register_5_q), .result(move_and_add_2_result), .current(register_4_q),
    .multiplier(register_6_q[1]), .moved_multiplicand(move_and_add_2_moved_multiplicand));
  Register register_7 (.D(move_and_add_2_result), .clk(CLK), .Q(register_7_q));  // open: en, clr
  Register register_8 (.D(move_and_add_2_moved_multiplicand), .clk(CLK), .Q(register_8_q));  // open: en, clr
  Register #(.width(4)) register_9 (.D(register_6_q), .clk(CLK), .Q(register_9_q));  // open: en, clr
  // Probe on register_8_q
  // Probe on register_7_q
  move_and_add move_and_add_3 (
    .multiplicand(register_8_q), .result(move_and_add_3_result), .current(register_7_q),
    .multiplier(register_9_q[2]), .moved_multiplicand(move_and_add_3_moved_multiplicand));
  Register register_10 (.D(move_and_add_3_result), .clk(CLK), .Q(register_10_q));  // open: en, clr
  Register register_11 (.D(move_and_add_3_moved_multiplicand), .clk(CLK), .Q(register_11_q));  // open: en, clr
  Register #(.width(4)) register_12 (.D(register_9_q), .clk(CLK), .Q(register_12_q));  // open: en, clr
  // Probe on register_11_q
  // Probe on register_10_q
  // Probe on out1
  move_and_add move_and_add_4 (
    .multiplicand(register_11_q), .result(out1), .current(register_10_q), .multiplier(register_12_q[3]));  // open: moved_multiplicand
endmodule

module move_and_add (
  input  [7:0] current,
  input  [7:0] multiplicand,
  input  multiplier,
  output [7:0] result,
  output [7:0] moved_multiplicand
);

  wire [7:0] multiplexer_1_out;

  Multiplexer #(.width(8), .enable("false")) multiplexer_1 (
    .in0({8{1'b0}}), .in1(multiplicand), .out(multiplexer_1_out), .sel(multiplier));
  Adder adder_1 (.a(current), .b(multiplexer_1_out), .out(result));  // open: cin, cout
  Shifter shifter_1 (.in(multiplicand), .\dist (3'b001), .out(moved_multiplicand));
endmodule
